# Fritzing sketch sketch (saved by Fritzing 0.9.3b)
breadboards: 1

parts:
  Part1 = Arduino Uno (Rev3)
  LED1 = RGB LED (com. cathode, rgb) [package="5 mm [THT]"]
  J1 = Basic Servo
  R1 = Resistor [tolerance=±5% resistance=220 package=THT]
  R2 = Resistor [tolerance=±5% resistance=220 package=THT]
  R3 = Resistor [tolerance=±5% resistance=220 package=THT]
  RE1 = Rotary Encoder [package=THT]
  hc-sr1 = hc-sr04
  J2 = Piezo Speaker
  R4 = Resistor [tolerance=±5% resistance=100 package="0603 [SMD]"]

nets:
  N1: Part1.D8, R1.Pin_0
  N2: Part1.D9_PWM, R2.Pin_0
  N3: Part1.D10_PWM/SS, R3.Pin_0
  N4: Part1.D11_PWM/MOSI, hc-sr1.Trig
  N5: Part1.D12/MISO, hc-sr1.Echo
  N6: Part1.D13/SCK, RE1.EncoderPinA
  N7: Part1.D6_PWM, J2.pin2
  N8: Part1.D7, J1.pulse
  VCC: Part1.5V, J1.vcc, RE1.EncoderPinC, hc-sr1.VCC
  GND: Part1.GND, LED1.common_cathode, J1.gnd, RE1.EncoderPinB, hc-sr1.GND, R4.Pin_0
  N9: LED1.red_anode, R1.Pin_1
  N10: LED1.green_anode, R2.Pin_1
  N11: LED1.blue_anode, R3.Pin_1
  N12: J2.pin1, R4.Pin_1
